# Fritzing sketch fritzing (saved by Fritzing 0.9.3b)
circuit board: 8.46667cm x 5.64444cm
breadboards: 1

parts:
  Componente1 = Arduino Nano (Rev3.0)
  KY-1 = Keyes Relay [package=THT]
  R1 = Photocell (LDR) [package=THT]
  DHT11_1 = DHT11 module  # not connected
  R2 = Resistor [tolerance=±5% resistance=10k package="2010 [SMD]"]
  Componente2 = Bluetooth HC-06

nets:
  N1: Componente1.D1/TX, Componente2.RXD
  N2: Componente1.D0/RX, Componente2.TXD
  GND: Componente1.GND, KY-1.ground, R2.Pin_0, Componente2.GND
  N3: Componente1.D9, KY-1.signal
  5V: Componente1.5V, KY-1.power, R1.pin_1, Componente2.VCC
  N4: Componente1.A7, R1.pin_0, R2.Pin_1

custom parts:
  Keyes Relay: The Keyes 5V relay module is suitable for SCM development, home appliance control. It uses a 5V~12V TIL control signal which can control DC / AC signal.
  DHT11 module: DHT11 black pcb module
